# Fritzing sketch sensor hub robot 2018 (saved by Fritzing 0.9.3b)
circuit board: 5.27546cm x 4.80277cm
breadboards: 1

parts:
  JP6 = Header 4 [package=jst-4-pth]
  JP5 = Header 4 [package=jst-4-pth]
  MUX1 = Adafruit TCA9548A
  JP3 = Header 4 [package=jst-4-pth]
  JP1 = Header 4 [package=jst-4-pth]
  JP4 = Header 4 [package=jst-4-pth]
  JP2 = Header 4 [package=jst-4-pth]
  JP7 = Header 4 [package=jst-4-pth]

nets:
  N1: JP6.1, JP5.1, MUX1.VCC, JP3.1, JP1.1, JP4.1, JP2.1, JP7.4
  N2: JP6.2, JP5.2, MUX1.GND, JP3.2, JP1.2, JP4.2, JP2.2, JP7.3
  N3: JP6.3, MUX1.5SDA
  N4: JP6.4, MUX1.5SCL
  N5: JP5.3, MUX1.4SDA
  N6: JP5.4, MUX1.4SCL
  N7: MUX1.2SDA, JP3.3
  N8: MUX1.2SCL, JP3.4
  N9: MUX1.3SDA, JP4.3
  N10: MUX1.3SCL, JP4.4
  N11: MUX1.INPUTSDA, JP7.2
  N12: MUX1.INPUTSCL, JP7.1
  N13: MUX1.0SDA, JP1.3
  N14: MUX1.0SCL, JP1.4
  N15: MUX1.1SDA, JP2.3
  N16: MUX1.1SCL, JP2.4

custom parts:
  Adafruit TCA9548A: You just found the perfect I2C sensor, and you want to wire up two or three or more of them to your Arduino when you realize "Uh oh, this chip has a fixed I2C address, and from what I know about I2C, you cannot have two devices with the same address on the same SDA/SCL pins!" Are you out of luck? You would be, if you didn't have this ultra-cool TCA9548A 1-to-8 I2C multiplexer! Finally, a way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
